# Fritzing sketch MusicalBattleshipCircuit (saved by Fritzing 0.9.6b)
breadboards: 1

parts:
  Mod1 = Raspberry Pi 4B
  PLAYER_1_BUTTONS = IC, DIP package, 28 pins [chip_label=MCP23017]
  PLAYER_2_BUTTONS1 = IC, DIP package, 28 pins [chip_label=MCP23017]
  7_SEGMENT_DISPLAY_OUTPUTS = IC, DIP package, 28 pins [chip_label=MCP23017]
  ANALOG_INPUTS = IC, DIP package, 16 pins [chip_label=MCP3008]
  R1 = Resistor [tolerance=±5% power=0.25 resistance=4.7k package=THT]  # not connected
  R2 = Resistor [tolerance=±5% power=0.25 resistance=4.7k package=THT]  # not connected
  R3 = Resistor [tolerance=±5% power=0.25 resistance=4.7k package=THT]  # not connected
  R4 = Resistor [tolerance=±5% power=0.25 resistance=4.7k package=THT]  # not connected
  R5 = Resistor [tolerance=±5% power=0.25 resistance=4.7k package=THT]  # not connected
  R6 = Resistor [tolerance=±5% power=0.25 resistance=4.7k package=THT]  # not connected
  C1 = Electrolytic Capacitor [capacitance=0.1µF voltage=50V package="100 mil [THT, electrolytic]"]  # not connected
  C2 = Electrolytic Capacitor [capacitance=0.1µF voltage=50V package="100 mil [THT, electrolytic]"]  # not connected
  C3 = Electrolytic Capacitor [capacitance=0.1µF voltage=50V package="100 mil [THT, electrolytic]"]  # not connected
  7_Segment_Numpers_P1 = 7 Segment Display
  R7 = Resistor [tolerance=±5% power=0.25 resistance=330 package=THT]
  R8 = Resistor [tolerance=±5% power=0.25 resistance=330 package=THT]
  R9 = Resistor [tolerance=±5% power=0.25 resistance=330 package=THT]
  R10 = Resistor [tolerance=±5% power=0.25 resistance=330 package=THT]
  R11 = Resistor [tolerance=±5% power=0.25 resistance=330 package=THT]
  R12 = Resistor [tolerance=±5% power=0.25 resistance=330 package=THT]
  R13 = Resistor [tolerance=±5% power=0.25 resistance=330 package=THT]
  7_Segment_Letters_P1 = 7 Segment Display
  R14 = Resistor [tolerance=±5% power=0.25 resistance=330 package=THT]
  R15 = Resistor [tolerance=±5% power=0.25 resistance=330 package=THT]
  R16 = Resistor [tolerance=±5% power=0.25 resistance=330 package=THT]
  R17 = Resistor [tolerance=±5% power=0.25 resistance=330 package=THT]
  R18 = Resistor [tolerance=±5% power=0.25 resistance=330 package=THT]
  R19 = Resistor [tolerance=±5% power=0.25 resistance=330 package=THT]
  R20 = Resistor [tolerance=±5% power=0.25 resistance=330 package=THT]
  7_Segment_Numbers_P2 = 7 Segment Display
  R21 = Resistor [tolerance=±5% power=0.25 resistance=330 package=THT]
  R22 = Resistor [tolerance=±5% power=0.25 resistance=330 package=THT]
  R23 = Resistor [tolerance=±5% power=0.25 resistance=330 package=THT]
  R24 = Resistor [tolerance=±5% power=0.25 resistance=330 package=THT]
  R25 = Resistor [tolerance=±5% power=0.25 resistance=330 package=THT]
  R26 = Resistor [tolerance=±5% power=0.25 resistance=330 package=THT]
  R27 = Resistor [tolerance=±5% power=0.25 resistance=330 package=THT]
  7_Segment_Letters_P2 = 7 Segment Display
  R28 = Resistor [tolerance=±5% power=0.25 resistance=330 package=THT]
  R29 = Resistor [tolerance=±5% power=0.25 resistance=330 package=THT]
  R30 = Resistor [tolerance=±5% power=0.25 resistance=330 package=THT]
  R31 = Resistor [tolerance=±5% power=0.25 resistance=330 package=THT]
  R32 = Resistor [tolerance=±5% power=0.25 resistance=330 package=THT]
  R33 = Resistor [tolerance=±5% power=0.25 resistance=330 package=THT]
  R34 = Resistor [tolerance=±5% power=0.25 resistance=330 package=THT]
  S1 = Pushbutton [package=THT]
  S2 = Pushbutton [package=THT]
  S3 = Pushbutton [package=THT]
  S4 = Pushbutton [package=THT]
  S5 = Pushbutton [package=THT]
  S6 = Pushbutton [package=THT]
  S7 = Pushbutton [package=THT]
  S8 = Pushbutton [package=THT]
  S9 = Pushbutton [package=THT]
  S10 = Pushbutton [package=THT]
  V1 = DC Power [voltage=5]
  R35 = Resistor [tolerance=±5% power=0.25 resistance=4.7k package=THT]
  R36 = Resistor [tolerance=±5% power=0.25 resistance=4.7k package=THT]
  V2 = DC Power [voltage=5]
  V3 = DC Power [voltage=5]
  R37 = Resistor [tolerance=±5% power=0.25 resistance=4.7k package=THT]
  S11 = Toggle Switch [package=THT]
  S12 = Pushbutton [package=THT]
  S13 = Pushbutton [package=THT]
  S14 = Pushbutton [package=THT]
  S15 = Pushbutton [package=THT]
  S16 = Pushbutton [package=THT]
  S17 = Pushbutton [package=THT]
  S18 = Pushbutton [package=THT]
  S19 = Pushbutton [package=THT]
  S20 = Pushbutton [package=THT]
  S21 = Pushbutton [package=THT]
  S22 = Toggle Switch [package=THT]
  P1_Slide = Slide Potentiometer [maximum_resistance=10kΩ]
  P1_Encoder = Rotary Encoder [package=THT]
  P2_Slide = Slide Potentiometer [maximum_resistance=10kΩ]
  P2_Encoder = Rotary Encoder [package=THT]
  S23 = Pushbutton [package=THT]
  S24 = Pushbutton [package=THT]

nets:
  N1: Mod1.3V3, PLAYER_1_BUTTONS.pin9, ANALOG_INPUTS.pin15, ANALOG_INPUTS.pin16, P1_Slide.leg1, P1_Encoder.EncoderPinB, P2_Slide.leg1, P2_Encoder.EncoderPinB
  N2: Mod1.GPIO2, PLAYER_1_BUTTONS.pin13
  N3: Mod1.GPIO3, PLAYER_1_BUTTONS.pin12
  N4: Mod1.GPIO4, R31.Pin_0
  N5: Mod1.GPIO17, R28.Pin_0
  N6: Mod1.GPIO18, R14.Pin_0
  N7: Mod1.GPIO27, R34.Pin_0
  N8: Mod1.GPIO22, R33.Pin_0
  N9: Mod1.GPIO23, R16.Pin_0
  N10: Mod1.GPIO24, R17.Pin_0
  N11: Mod1.GPIO10, ANALOG_INPUTS.pin11
  N12: Mod1.GPIO9, ANALOG_INPUTS.pin12
  N13: Mod1.GPIO25, R18.Pin_0
  N14: Mod1.GPIO11, ANALOG_INPUTS.pin13
  N15: Mod1.GPIO8, ANALOG_INPUTS.pin10
  N16: Mod1.GPIO6, R29.Pin_0
  N17: Mod1.GPIO12, R15.Pin_0
  N18: Mod1.GPIO13, R32.Pin_0
  N19: Mod1.GPIO19, R30.Pin_0
  N20: Mod1.GPIO16, R19.Pin_0
  N21: Mod1.GPIO26, S24.leg0
  N22: Mod1.GPIO20, R20.Pin_0
  N23: Mod1.GPIO21, S23.leg0
  N24: PLAYER_1_BUTTONS.pin1, S9.leg0
  N25: PLAYER_1_BUTTONS.pin2, S10.leg0
  N26: PLAYER_1_BUTTONS.pin3, S11.L2
  N27: PLAYER_1_BUTTONS.pin4, S11.L1
  GND: PLAYER_1_BUTTONS.pin15, PLAYER_1_BUTTONS.pin16, PLAYER_1_BUTTONS.pin17, PLAYER_2_BUTTONS1.pin16, PLAYER_2_BUTTONS1.pin17, 7_SEGMENT_DISPLAY_OUTPUTS.pin10, 7_SEGMENT_DISPLAY_OUTPUTS.pin15, 7_SEGMENT_DISPLAY_OUTPUTS.pin17, ANALOG_INPUTS.pin9, ANALOG_INPUTS.pin14, 7_Segment_Numpers_P1.common_anode, 7_Segment_Letters_P1.common_anode, 7_Segment_Numbers_P2.common_anode, 7_Segment_Letters_P2.common_anode, S1.leg1, S2.leg1, S3.leg1, S4.leg1, S5.leg1, S6.leg1, S7.leg1, S8.leg1, S9.leg1, S10.leg1, S11.COM, S12.leg1, S13.leg1, S14.leg1, S15.leg1, S16.leg1, S17.leg1, S18.leg1, S19.leg1, S20.leg1, S21.leg1, S22.COM, P1_Slide.leg2, P1_Encoder.EncoderPinA, P2_Slide.leg2, P2_Encoder.EncoderPinA, S23.leg1, S24.leg1
  N28: PLAYER_1_BUTTONS.pin21, S1.leg0
  N29: PLAYER_1_BUTTONS.pin22, S2.leg0
  N30: PLAYER_1_BUTTONS.pin23, S3.leg0
  N31: PLAYER_1_BUTTONS.pin24, S4.leg0
  N32: PLAYER_1_BUTTONS.pin25, S5.leg0
  N33: PLAYER_1_BUTTONS.pin26, S6.leg0
  N34: PLAYER_1_BUTTONS.pin27, S7.leg0
  N35: PLAYER_1_BUTTONS.pin28, S8.leg0
  N36: PLAYER_2_BUTTONS1.pin1, S17.leg0
  N37: PLAYER_2_BUTTONS1.pin2, S15.leg0
  N38: PLAYER_2_BUTTONS1.pin3, S22.L2
  N39: PLAYER_2_BUTTONS1.pin4, S22.L1
  N40: PLAYER_2_BUTTONS1.pin15, 7_SEGMENT_DISPLAY_OUTPUTS.pin9, 7_SEGMENT_DISPLAY_OUTPUTS.pin16
  N41: PLAYER_2_BUTTONS1.pin21, S12.leg0
  N42: PLAYER_2_BUTTONS1.pin22, S19.leg0
  N43: PLAYER_2_BUTTONS1.pin23, S18.leg0
  N44: PLAYER_2_BUTTONS1.pin24, S16.leg0
  N45: PLAYER_2_BUTTONS1.pin25, S13.leg0
  N46: PLAYER_2_BUTTONS1.pin26, S21.leg0
  N47: PLAYER_2_BUTTONS1.pin27, S14.leg0
  N48: PLAYER_2_BUTTONS1.pin28, S20.leg0
  N49: 7_SEGMENT_DISPLAY_OUTPUTS.pin1, R26.Pin_0
  N50: 7_SEGMENT_DISPLAY_OUTPUTS.pin2, R27.Pin_0
  N51: 7_SEGMENT_DISPLAY_OUTPUTS.pin3, R22.Pin_0
  N52: 7_SEGMENT_DISPLAY_OUTPUTS.pin4, R25.Pin_0
  N53: 7_SEGMENT_DISPLAY_OUTPUTS.pin5, R24.Pin_0
  N54: 7_SEGMENT_DISPLAY_OUTPUTS.pin6, R21.Pin_0
  N55: 7_SEGMENT_DISPLAY_OUTPUTS.pin7, R23.Pin_0
  N56: 7_SEGMENT_DISPLAY_OUTPUTS.pin21, R7.Pin_0
  N57: 7_SEGMENT_DISPLAY_OUTPUTS.pin22, R8.Pin_0
  N58: 7_SEGMENT_DISPLAY_OUTPUTS.pin23, R9.Pin_0
  N59: 7_SEGMENT_DISPLAY_OUTPUTS.pin24, R10.Pin_0
  N60: 7_SEGMENT_DISPLAY_OUTPUTS.pin25, R11.Pin_0
  N61: 7_SEGMENT_DISPLAY_OUTPUTS.pin26, R12.Pin_0
  N62: 7_SEGMENT_DISPLAY_OUTPUTS.pin27, R13.Pin_0
  N63: ANALOG_INPUTS.pin1, P1_Slide.wiper
  N64: ANALOG_INPUTS.pin2, P1_Encoder.EncoderPinC
  N65: ANALOG_INPUTS.pin3, P2_Slide.wiper
  N66: ANALOG_INPUTS.pin4, P2_Encoder.EncoderPinC
  N67: V1.V+, R35.Pin_1
  N68: R36.Pin_1, V2.V+
  N69: V3.V+, R37.Pin_1
